# Fritzing sketch MoistureSensor (saved by Fritzing 0.9.3b)
breadboards: 1

parts:
  Raspberry_Pi_1 = Raspberry Pi 3 [part_number=RPI-3-V1.2]
  IC1 = MCP3008 8-channel 10-bit ADC [part_number=MCP3008]
  Part1 = Soil Moisture Sensor

nets:
  N1: Raspberry_Pi_1.3v3, IC1.no_name_yet#15, IC1.no_name_yet#16
  N2: Raspberry_Pi_1.GPIO22, Part1.VCC
  N3: Raspberry_Pi_1.GPIO25, IC1.no_name_yet#13
  N4: Raspberry_Pi_1.GPIO24, IC1.no_name_yet#12
  N5: Raspberry_Pi_1.GPIO23, IC1.no_name_yet#11
  N6: Raspberry_Pi_1.GPIO18, IC1.no_name_yet#10
  GND: Raspberry_Pi_1.GND, IC1.no_name_yet#9, IC1.no_name_yet#14, Part1.GND
  N7: IC1.no_name_yet#6, Part1.SIG

notes:
  3.3V
